# Fritzing sketch Analog_Joystick (saved by Fritzing 0.9.3b)
breadboards: 1

parts:
  Mod1 = Raspberry Pi Pico W
  S1 = Pushbutton [package="[SMD]"]
  S2 = Pushbutton [package="[SMD]"]
  Part1 = Thumb Joystick

nets:
  N1: Mod1.pin_3, Mod1.pin_8, Mod1.pin_13, Mod1.pin_18, Mod1.pin_23, Mod1.pin_28, Mod1.pin_33, Mod1.pin_38, S1.Pin_1, S1.Pin_2, S2.Pin_1, S2.Pin_2, Part1.GND
  N2: Mod1.pin_9, S1.Pin_3, S1.Pin_4
  N3: Mod1.pin_10, S2.Pin_3, S2.Pin_4
  N4: Mod1.pin_29, Part1.SEL
  N5: Mod1.pin_31, Part1.HORZ
  N6: Mod1.pin_32, Part1.VERT
  N7: Mod1.pin_36, Part1.VCC

custom parts:
  Raspberry Pi Pico W: Raspberry Pi Pico W. Based around the RP2040 microcontroller the Pico W is a low cost microcontroller device bringing Raspberry Pi quality, cost, and easy of use to the microcontroller space. The areas marked KEEPOUT in pcb silkscreen should not have traces running through them to avoid shorts on a soldered in module!
