# Fritzing sketch Attendence (saved by Fritzing 0.9.3b)
breadboards: 1

parts:
  Display_LCD_16x2 = LCD Display 16x2
  Convertitore_Expander_seriale = LCM1602 IIC [chip_label="Modulo " part_number="LCM1602 IIC" package="DIP (Dual Inline) [THT]"]
  MH-Real-Time_Clock_Module_2 = RTC_DS1302_module
  Part1 = RFID-RC522-v2
  Mod1 = Raspberry Pi Pico W
  S1 = Momentary Switch [package=ksa_sealed_tac_switch]
  LED1 = RGB LED (com. anode, rbg) [package="5 mm [THT]"]
  SG1 = Buzzer 12mm [package=buzzer-12mm-ns]
  SG2 = Buzzer 12mm [package=buzzer-12mm-ns]

nets:
  N1: Display_LCD_16x2.aún_sin_nombre#0, Convertitore_Expander_seriale.VSS
  N2: Display_LCD_16x2.aún_sin_nombre#1, Convertitore_Expander_seriale.VDD
  N3: Display_LCD_16x2.aún_sin_nombre#2, Convertitore_Expander_seriale.V0
  N4: Display_LCD_16x2.aún_sin_nombre#3, Convertitore_Expander_seriale.RS
  N5: Display_LCD_16x2.aún_sin_nombre#4, Convertitore_Expander_seriale.RW
  N6: Display_LCD_16x2.aún_sin_nombre#5, Convertitore_Expander_seriale.E
  N7: Display_LCD_16x2.aún_sin_nombre#6, Convertitore_Expander_seriale.D0
  N8: Display_LCD_16x2.aún_sin_nombre#7, Convertitore_Expander_seriale.D1
  N9: Display_LCD_16x2.aún_sin_nombre#8, Convertitore_Expander_seriale.D2
  N10: Display_LCD_16x2.aún_sin_nombre#9, Convertitore_Expander_seriale.D3
  N11: Display_LCD_16x2.aún_sin_nombre#10, Convertitore_Expander_seriale.D4
  N12: Display_LCD_16x2.aún_sin_nombre#11, Convertitore_Expander_seriale.D5
  N13: Display_LCD_16x2.aún_sin_nombre#12, Convertitore_Expander_seriale.D6
  N14: Display_LCD_16x2.aún_sin_nombre#13, Convertitore_Expander_seriale.D7
  N15: Display_LCD_16x2.aún_sin_nombre#14, Convertitore_Expander_seriale.A
  N16: Display_LCD_16x2.aún_sin_nombre#15, Convertitore_Expander_seriale.K
  GND: Convertitore_Expander_seriale.GND, MH-Real-Time_Clock_Module_2.GND, Part1.GND, Mod1.pin_3, Mod1.pin_8, Mod1.pin_13, Mod1.pin_18, Mod1.pin_23, Mod1.pin_28, Mod1.pin_33, Mod1.pin_38, Mod1.pin_42, S1.2, LED1.green_cathode, SG1.1, SG2.1
  N17: Convertitore_Expander_seriale.VCC, Mod1.pin_40
  N18: Convertitore_Expander_seriale.SDA, Mod1.pin_14
  N19: Convertitore_Expander_seriale.SCL, Mod1.pin_15
  N20: Convertitore_Expander_seriale.LED_A, Convertitore_Expander_seriale.LED_B
  VCC: MH-Real-Time_Clock_Module_2.VCC, Part1.3.3V, Mod1.pin_36
  N21: MH-Real-Time_Clock_Module_2.RST, Mod1.pin_24
  N22: MH-Real-Time_Clock_Module_2.DAT, Mod1.pin_22
  N23: MH-Real-Time_Clock_Module_2.CLK, Mod1.pin_21
  N24: Part1.SDA, Mod1.pin_2
  N25: Part1.SCK, Mod1.pin_4
  N26: Part1.MOSI, Mod1.pin_5
  N27: Part1.MISO, Mod1.pin_6
  N28: Part1.IRQ, Mod1.pin_7
  N29: Part1.RST, Mod1.pin_1
  N30: Mod1.pin_17, LED1.blue_cathode
  N31: Mod1.pin_19, LED1.red_cathode
  N32: Mod1.pin_20, LED1.common_anode
  N33: Mod1.pin_25, SG1.2
  N34: Mod1.pin_26, SG2.2
  N35: Mod1.pin_30, S1.3

custom parts:
  LCM1602 IIC: I2C-Module to use a 1602 or 2004 LCD on with the wire.h libory Serial LCD Modul
  RTC_DS1302_module: Arduino module DS1302 SPI Real Time Clock
  RFID-RC522-v2: A simple China made RFID-RC522 Reader; do check the pin labels, as this is a MFRC522 based clone.
  Raspberry Pi Pico W: Raspberry Pi Pico W. Based around the RP2040 microcontroller the Pico W is a low cost microcontroller device bringing Raspberry Pi quality, cost, and easy of use to the microcontroller space. The areas marked KEEPOUT in pcb silkscreen should not have traces running through them to avoid shorts on a soldered in module!
