# Fritzing sketch GroupProject (saved by Fritzing 0.9.3b)
breadboards: 1

parts:
  Mod1 = Raspberry Pi Pico W
  WeMos_D1_Mini_Relay_Shield1 = WeMos D1 Mini Relay Shield
  R1 = Resistor [tolerance=±5% resistance=1k package="2010 [SMD]"]
  Part1 = Adafruit PDM Mic with JST [part_number="Adafruit #4346"]
  M1 = DC Motor
  LCD2004-I2C1 = LCD2004-I2C
  Load_Cell1 = Load Cell - Red/white/black/green
  Part2 = I2C level shifter bidirectional
  U1 = LIPO-110mAh [package=lipo-110]

nets:
  N1: Mod1.pin_1, Part2.LV1
  N2: Mod1.pin_2, Part2.LV2
  GND: Mod1.pin_3, Mod1.pin_8, Mod1.pin_13, Mod1.pin_18, Mod1.pin_23, Mod1.pin_28, Mod1.pin_33, Mod1.pin_38, Mod1.pin_42, R1.Pin_0, Part1.GND, LCD2004-I2C1.GND, Load_Cell1.wire3, Part2.GND
  N3: Mod1.pin_4, WeMos_D1_Mini_Relay_Shield1.D4
  N4: Mod1.pin_19, Load_Cell1.wire4
  N5: Mod1.pin_20, Load_Cell1.wire2
  N6: Mod1.pin_24, Mod1.pin_25, Part1.DATA, Part1.CLK
  5V: Mod1.pin_40, WeMos_D1_Mini_Relay_Shield1.5V, Part1.VDD, Load_Cell1.wire1, Part2.LV
  N7: WeMos_D1_Mini_Relay_Shield1.COM, M1.pin_2
  N8: WeMos_D1_Mini_Relay_Shield1.G, R1.Pin_1
  N9: WeMos_D1_Mini_Relay_Shield1.NO, U1.+
  N10: M1.pin_1, U1.-
  N11: LCD2004-I2C1.VCC, Part2.HV
  N12: LCD2004-I2C1.SDA, Part2.HV1
  N13: LCD2004-I2C1.SCL, Part2.HV2

custom parts:
  Raspberry Pi Pico W: Raspberry Pi Pico W. Based around the RP2040 microcontroller the Pico W is a low cost microcontroller device bringing Raspberry Pi quality, cost, and easy of use to the microcontroller space. The areas marked KEEPOUT in pcb silkscreen should not have traces running through them to avoid shorts on a soldered in module!
  LCD2004-I2C: A standard character display with 4x20 characters. Comes in many colors with LCM2004 IIC attached.
  Load Cell - Red/white/black/green: A rectangle load cell/weighting pressure Sensor with four wires - Red, white, black, green. Normally corresponding with E+, E-, A+, A- respectively.
