# Fritzing sketch Temperatuur-LCD-RTC (saved by Fritzing 0.9.3b)
breadboards: 1

parts:
  Convertitore_Expander_seriale = LCM1602 IIC [chip_label="Modulo " part_number="LCM1602 IIC" package="DIP (Dual Inline) [THT]"]
  part = RTC_DS1302_module
  part_2 = LCD Display 16x2
  Mod1 = Raspberry Pi Pico W
  M1 = Humidity and Temperature Sensor DHT11
  S1 = Momentary Switch [package=ksa_sealed_tac_switch]

nets:
  N1: Convertitore_Expander_seriale.VSS, part_2.aún_sin_nombre#0
  N2: Convertitore_Expander_seriale.VDD, part_2.aún_sin_nombre#1
  N3: Convertitore_Expander_seriale.V0, part_2.aún_sin_nombre#2
  N4: Convertitore_Expander_seriale.RS, part_2.aún_sin_nombre#3
  N5: Convertitore_Expander_seriale.RW, part_2.aún_sin_nombre#4
  N6: Convertitore_Expander_seriale.E, part_2.aún_sin_nombre#5
  N7: Convertitore_Expander_seriale.D0, part_2.aún_sin_nombre#6
  N8: Convertitore_Expander_seriale.D1, part_2.aún_sin_nombre#7
  N9: Convertitore_Expander_seriale.D2, part_2.aún_sin_nombre#8
  N10: Convertitore_Expander_seriale.D3, part_2.aún_sin_nombre#9
  N11: Convertitore_Expander_seriale.D4, part_2.aún_sin_nombre#10
  N12: Convertitore_Expander_seriale.D5, part_2.aún_sin_nombre#11
  N13: Convertitore_Expander_seriale.D6, part_2.aún_sin_nombre#12
  N14: Convertitore_Expander_seriale.D7, part_2.aún_sin_nombre#13
  N15: Convertitore_Expander_seriale.A, part_2.aún_sin_nombre#14
  N16: Convertitore_Expander_seriale.K, part_2.aún_sin_nombre#15
  GND: Convertitore_Expander_seriale.GND, part.GND, Mod1.pin_3, Mod1.pin_8, Mod1.pin_13, Mod1.pin_18, Mod1.pin_23, Mod1.pin_28, Mod1.pin_33, Mod1.pin_38, Mod1.pin_42, M1.NC, S1.2
  N17: Convertitore_Expander_seriale.VCC, Mod1.pin_40
  N18: Convertitore_Expander_seriale.SDA, Mod1.pin_1
  N19: Convertitore_Expander_seriale.SCL, Mod1.pin_2
  N20: Convertitore_Expander_seriale.LED_A, Convertitore_Expander_seriale.LED_B
  N21: part.VCC, Mod1.pin_36, M1.Data
  N22: part.RST, Mod1.pin_21
  N23: part.DAT, Mod1.pin_22
  N24: part.CLK, Mod1.pin_24
  N25: Mod1.pin_20, M1.Vcc
  N26: Mod1.pin_30, S1.3

custom parts:
  LCM1602 IIC: I2C-Module to use a 1602 or 2004 LCD on with the wire.h libory Serial LCD Modul
  RTC_DS1302_module: Arduino module DS1302 SPI Real Time Clock
  Raspberry Pi Pico W: Raspberry Pi Pico W. Based around the RP2040 microcontroller the Pico W is a low cost microcontroller device bringing Raspberry Pi quality, cost, and easy of use to the microcontroller space. The areas marked KEEPOUT in pcb silkscreen should not have traces running through them to avoid shorts on a soldered in module!
  Humidity and Temperature Sensor DHT11: Digital relative humidity & temperature sensor DHT11
