# Fritzing sketch Voltmeter (saved by Fritzing 0.9.3b)
breadboards: 2

parts:
  R1 = Resistor [tolerance=±5% resistance=220 package=THT]
  R2 = Resistor [tolerance=±5% resistance=220 package=THT]
  R3 = Resistor [tolerance=±5% resistance=220 package=THT]
  Mod1 = Raspberry Pi Pico W
  LED1 = 7-SEGMENT-4DIGIT-YOUNGSUN [package=7-segment-4digit-youngsun-longpads]
  R4 = Resistor [tolerance=±5% resistance=220 package=THT]
  R5 = Resistor [tolerance=±5% resistance=220 package=THT]
  R6 = Resistor [tolerance=±5% resistance=220 package=THT]
  R7 = Resistor [tolerance=±5% resistance=220 package=THT]
  R8 = Resistor [tolerance=±5% resistance=220 package=THT]
  R9 = Resistor [tolerance=±5% resistance=220 package=THT]
  R10 = Resistor [tolerance=±5% resistance=220 package=THT]
  Q1 = NPN-Transistor [package="TO92 [THT]"]
  Q2 = NPN-Transistor [package="TO92 [THT]"]
  Q3 = NPN-Transistor [package="TO92 [THT]"]
  Q4 = NPN-Transistor [package="TO92 [THT]"]
  R11 = Resistor [tolerance=±5% resistance=1k package=THT]
  R12 = Resistor [tolerance=±5% resistance=1k package=THT]
  R13 = Resistor [tolerance=±5% resistance=1k package=THT]
  R14 = Resistor [tolerance=±5% resistance=1k package=THT]
  BAT1 = BATTERY-2 [package=battery-aaa]
  R15 = Resistor [tolerance=±5% resistance=220 package=THT]

nets:
  N1: R1.Pin_1, R2.Pin_0
  N2: R2.Pin_1, R3.Pin_0, Mod1.pin_31
  N3: R3.Pin_1, Mod1.pin_3, Mod1.pin_8, Mod1.pin_13, Mod1.pin_18, Mod1.pin_23, Mod1.pin_28, Mod1.pin_33, Mod1.pin_38, Mod1.pin_42, Q1.C, Q2.C, Q3.C, Q4.C, BAT1.-1
  N4: Mod1.pin_1, R4.Pin_1
  N5: Mod1.pin_2, R6.Pin_1
  N6: Mod1.pin_4, R5.Pin_1
  N7: Mod1.pin_5, R7.Pin_1
  N8: Mod1.pin_6, R8.Pin_1
  N9: Mod1.pin_7, R9.Pin_1
  N10: Mod1.pin_9, R10.Pin_1
  N11: Mod1.pin_10, R14.Pin_1
  N12: Mod1.pin_11, R13.Pin_1
  N13: Mod1.pin_12, R12.Pin_1
  N14: Mod1.pin_14, R11.Pin_1
  N15: Mod1.pin_15, R15.Pin_1
  N16: LED1.DIG1, R8.Pin_0
  N17: LED1.DIG2, R7.Pin_0
  N18: LED1.D, R15.Pin_0
  N19: LED1.COL-A, R5.Pin_0
  N20: LED1.E, R10.Pin_0
  N21: LED1.DIG3, Q4.E
  N22: LED1.F, R6.Pin_0
  N23: LED1.COL-C, Q3.E
  N24: LED1.C, Q2.E
  N25: LED1.A, R9.Pin_0
  N26: LED1.G, R4.Pin_0
  N27: LED1.B, Q1.E
  N28: Q1.B, R14.Pin_0
  N29: Q2.B, R13.Pin_0
  N30: Q3.B, R12.Pin_0
  N31: Q4.B, R11.Pin_0

custom parts:
  Raspberry Pi Pico W: Raspberry Pi Pico W. Based around the RP2040 microcontroller the Pico W is a low cost microcontroller device bringing Raspberry Pi quality, cost, and easy of use to the microcontroller space. The areas marked KEEPOUT in pcb silkscreen should not have traces running through them to avoid shorts on a soldered in module!
