# Fritzing sketch Webserver (saved by Fritzing 0.9.3b)
breadboards: 1

parts:
  Mod1 = Raspberry Pi Pico W
  M1 = Humidity and Temperature Sensor DHT11
  WeMos_D1_Mini_Relay_Shield1 = WeMos D1 Mini Relay Shield

nets:
  N1: Mod1.pin_3, Mod1.pin_8, Mod1.pin_13, Mod1.pin_18, Mod1.pin_23, Mod1.pin_28, Mod1.pin_33, Mod1.pin_38, Mod1.pin_42, M1.NC, WeMos_D1_Mini_Relay_Shield1.G
  N2: Mod1.pin_20, M1.Vcc
  N3: Mod1.pin_21, WeMos_D1_Mini_Relay_Shield1.D2
  N4: Mod1.pin_36, M1.Data
  N5: Mod1.pin_40, WeMos_D1_Mini_Relay_Shield1.5V

custom parts:
  Raspberry Pi Pico W: Raspberry Pi Pico W. Based around the RP2040 microcontroller the Pico W is a low cost microcontroller device bringing Raspberry Pi quality, cost, and easy of use to the microcontroller space. The areas marked KEEPOUT in pcb silkscreen should not have traces running through them to avoid shorts on a soldered in module!
  Humidity and Temperature Sensor DHT11: Digital relative humidity & temperature sensor DHT11
